# Fritzing sketch ICcompletoRoteado2 (saved by Fritzing 0.9.3b)
circuit board: 9.19936cm x 7.66267cm
breadboards: 1

parts:
  Componente1 = Arduino Uno (Rev3)
  Leitor_biometrico = Humidity and Temperature Sensor RHT03
  BAT1 = BC9VPC [package=bc9vpc]
  JP1 = Header 4 [package=screwterminal-3.5mm-4_lock]
  R3 = Resistor [tolerance=±5% resistance=220 package="2010 [SMD]"]
  R2 = Resistor [tolerance=±5% resistance=220 package="2010 [SMD]"]
  R1 = Resistor [tolerance=±5% resistance=220 package="2010 [SMD]"]
  Leitor_SD = MicroSD Card Module
  LCD1 = LCD screen

nets:
  N1: Componente1.A4/SDA, JP1.3
  N2: Componente1.A5/SCL, JP1.4
  N3: Componente1.D8, Leitor_biometrico.GND_1
  N4: Componente1.D9_PWM, Leitor_biometrico.GND_2
  N5: Componente1.D10_PWM/SS, Leitor_SD.CS
  N6: Componente1.D11_PWM/MOSI, Leitor_SD.MISO
  N7: Componente1.D12/MISO, Leitor_SD.MOSI
  N8: Componente1.D13/SCK, Leitor_SD.SCK
  GND: Componente1.GND, Leitor_biometrico.Data-signal, BAT1.V-, JP1.1, R1.Pin_1, Leitor_SD.GND, LCD1.VSS, LCD1.R/W, LCD1.LED-
  N9: Componente1.D2, LCD1.DB7
  N10: Componente1.D3_PWM, LCD1.DB6
  N11: Componente1.D4, LCD1.DB5
  N12: Componente1.D5_PWM, LCD1.DB4
  N13: Componente1.D6_PWM, LCD1.E
  N14: Componente1.D7, LCD1.RS
  VCC: Componente1.5V, Leitor_biometrico.Vcc, JP1.2, R3.Pin_1, R2.Pin_1, Leitor_SD.VCC, LCD1.VDD
  N15: Componente1.VIN, BAT1.V+
  N16: R3.Pin_0, LCD1.LED+
  N17: R2.Pin_0, R1.Pin_0

notes:
  FEM - Unicamp

// code stored in the sketch: ICcompleto.ino
/*
 *
 * Desenvolvido por Bruno Oliveira - bruno97br@gmail.com
 *  Ultimo update - 01/03/2017
 *
 * Infos:
 *      RTC:
 *          https://www.filipeflop.com/blog/relogio-rtc-ds1307-arduino/
 *      Biometrico:
 *          http://blog.usinainfo.com.br/leitor-biometrico-arduino-sistema-de-cadastramento-e-leitura-de-digitais/
 *      CartaoSD:
 *          https://www.filipeflop.com/blog/cartao-sd-com-arduino/
 *      LCD:
 *          Arquvos exemplos do Arduino IDE
 */


 /*  TODO:
  *    Criar uma nova enroll q salve num txt a lista de IDs e RAs
  *    Criar funcao q importe os IDs e RAs dum txt
  *     
 */
#include <LiquidCrystal.h>

typedef struct aluno{
  short int ID;
  long RA;
} Aluno;

long professores[] = {0};

Aluno sala[] = {
                {0,0},
                {1,165215},
                {2,165216},
                {3,165217},
                {4,165215},
                {5,165216},
                {6,165217},
                {7,165215},
                {8,165216},
                {9,165217}
                };
//Global Var
String dataHj;
long ultimoCadastrado;
LiquidCrystal lcd(7, 6, 5, 4, 3, 2);
/****************************************************************************/

void setup() {
  long leitura;
  
  inicializarPerifericos();
  delay(100);
  report("Esperando professor");
  
  do{
    leitura = digitalLida();
    if(!ehProfessor(leitura)){
      report("Digital invalida");
      delay(700);
      report("Esperando professor");  
    }
    delay(100);
  }while(!ehProfessor(leitura));
  iniciarDia();
}

void loop() {
  delay(1000);
  report("Esperando digital");
  
  long leitura = digitalLida();
  
  if(valido(leitura)){  
    if(ehProfessor(leitura)){
      encerrarDia();
    }
    else{
     bool ok = gravarPresenca(leitura, dataHj);
     if(ok){
       report("Aluno " + String(leitura) + " presente!");
     }
    }
  }
  else{
    report("Problema ao ler digital");
  }
}

//Funções auxiliares
long digitalLida(){
  int IDlido;

  while(Serial.available() <= 0){
    delay(100);
  }

  IDlido = int(Serial.read()) - '0'; //---------------------------------------FLAG LEITORBIOMETRICO-----------
  
  while(Serial.available() > 0){
    char flush = Serial.read();
    delay(10);
  }
  if(IDlido >= (sizeof( sala ) / sizeof( sala[0] )) || IDlido < 0)
    return -1;
  return sala[IDlido].RA;
}

bool gravarPresenca(long leitura, String data){
  //Insere o RA e a data da presenca no arquivo aberto
  if(jaCadastrado(leitura)){
    report("Presenca ja cadastrada");
    return false;
  }
  else{
    Serial.print("Mensagem gravada no cartao: "); //---------------------------------------FLAG SD CARD-----------
    Serial.print(String(leitura));
    Serial.print(" ");
    Serial.println(data);
    return true;
  }
}

void iniciarDia(){
  dataHj = word(analogRead(A0)); //---------------------------------------FLAG RTC-----------
  report("Inicio do programa");
  delay(1000);
  report("Esperando digital");
}

void encerrarDia(){
  report("Fim do dia");
  Serial.end();
  delay(1000);
  asm volatile ("  jmp 0");
}

void report(String message){
  String linhas[2];
  quebra(message,linhas);
  lcd.clear();
  lcd.setCursor(0,0);
  lcd.print(linhas[0]);
  lcd.setCursor(0,1);
  lcd.print(linhas[1]);
}

void inicializarPerifericos(){ //---------------------------------------FLAG all setups-----------
  String dataHj = "inicio";
  Serial.begin(9600);
  lcd.begin(16, 2);
}

bool jaCadastrado(long aluno){
  if(ultimoCadastrado == aluno)
    return true;
  ultimoCadastrado = aluno;
  return false;
}

void quebra(String message, String linhas[]) {
  int i;
  for(i=16;i>=0;i--){
    if(message[i] == ' ')
      break;
  }
  linhas[0] = (message.substring(0,i));
  linhas[1] = (message.substring(i+1));
}

bool ehProfessor(long candidato){
  int tamanho = (sizeof( professores ) / sizeof( professores[0] ));
  for(int i=0; i<tamanho; i++){
    if(candidato == professores[i])
      return true;
    }
  return false;
}

bool valido(long RA){
  if(RA < 0)
    return false;
  return true;  
}
